# Fritzing sketch SCTA Layout and Wiring (saved by Fritzing 1.0.4)
breadboards: 1

parts:
  A1 = Particle - Photon2
  M1 = Dagu DGServo 9g (Top view) [part_number=RS001B]
  IR1 = TSOP312.., 314.. [package=THT]
  OLED_I2C1 = OLED 128x64 I2C Monochrome Display
  J2 = Piezo Speaker
  S1 = Square Pushbutton

nets:
  N1: A1.Pin_2, IR1.Vs, OLED_I2C1.VDD, J2.pin2, S1.leg1
  GND: A1.Pin_4, M1.gnd, IR1.GND, OLED_I2C1.GND
  N2: A1.Pin_7, J2.pin1
  N3: A1.Pin_8, M1.pulse
  N4: A1.Pin_17, OLED_I2C1.SDA
  N5: A1.Pin_18, OLED_I2C1.SCK
  N6: A1.Pin_20, S1.leg0
  N7: A1.Pin_22, IR1.Data
  N8: A1.Pin_26, M1.vcc

custom parts:
  Particle - Photon2: The Photon 2 is a microcontroller and Wi-Fi networking developed by particle. Features: 802.11a/b/g/n Wi-Fi, 2.4 GHz and 5 GHz Integrated PCB antenna Integrated U.FL connector for external antenna Integrated RF switch BLE 5 using same antenna as Wi-Fi Realtek RTL8721DM MCU ARM Cortex M33 CPU, 200 MHz 2048 KB (2 MB) user application maximum size 3072 KB (3 MB) of RAM available to user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
